// Logisim project CSE_332_LAB_GROUP_NO_05_MID_TERM_EXAM_SECTION_NO_01.circ as structural Verilog: 1 circuit, main circuit main
module main (
  input  in_1,
  input  in_2,
  input  in_3,
  input  in_4,
  output D,
  output C,
  output B,
  output A
);

  wire and_1_out, and_2_out, and_3_out, and_4_out, and_5_out, and_6_out, and_7_out, and_8_out, clock_1_out,
       d_ff_1_qn, d_ff_2_qn, d_ff_3_qn, d_ff_4_qn, not_1_out, or_1_out, or_2_out, or_3_out, or_4_out,
       xor_1_out, xor_2_out, xor_3_out, xor_4_out;

  not not_1 (not_1_out, in_1);
  or or_1 (or_1_out, in_1, and_1_out);
  and and_1 (and_1_out, not_1_out, in_2);
  and and_2 (and_2_out, and_1_out, d_ff_1_qn);
  and and_3 (and_3_out, and_2_out, d_ff_2_qn);
  and and_4 (and_4_out, and_3_out, d_ff_3_qn);
  and and_5 (and_5_out, and_4_out, d_ff_4_qn);
  and and_6 (and_6_out, in_1, and_6_out);
  and and_7 (and_7_out, and_6_out, and_7_out);
  and and_8 (and_8_out, and_7_out, and_8_out);
  and and_9 (and_5_out, and_8_out, and_5_out);
  xor xor_1 (xor_1_out, and_6_out, or_1_out);
  or or_2 (or_2_out, and_2_out, and_6_out);
  or or_3 (or_3_out, and_3_out, and_7_out);
  or or_4 (or_4_out, and_4_out, and_8_out);
  xor xor_2 (xor_2_out, and_7_out, or_2_out);
  xor xor_3 (xor_3_out, and_8_out, or_3_out);
  xor xor_4 (xor_4_out, and_5_out, or_4_out);
  Clock clock_1 (.out(clock_1_out));
  D_Flip_Flop d_ff_1 (.D(xor_1_out), .clk(clock_1_out), .Q(D), .Qn(d_ff_1_qn), .preset(xor_2_out), .reset(xor_2_out));
  D_Flip_Flop d_ff_2 (.D(xor_2_out), .clk(clock_1_out), .Q(C), .Qn(d_ff_2_qn), .preset(xor_2_out), .reset(xor_2_out));
  D_Flip_Flop d_ff_3 (.D(xor_3_out), .clk(clock_1_out), .Q(B), .Qn(d_ff_3_qn), .preset(xor_2_out), .reset(xor_2_out));
  D_Flip_Flop d_ff_4 (.D(xor_4_out), .clk(clock_1_out), .Q(A), .Qn(d_ff_4_qn), .preset(xor_2_out), .reset(xor_2_out));
endmodule
